# Fritzing sketch ArdIllu (saved by Fritzing 0.9.6b)
stripboards: 1

parts:
  IC2 = IC, DIP package, 16 pins [chip_label=MAX4618]
  Part1 = Arduino Nano (Rev3.0)
  J1 = Power Jack [package=power_jack_pth]
  U1 = MCP6241 [part_number=MCP6241 package=dip08]
  U2 = BNC [package=bnc]
  R1 = Resistor [tolerance=±5% resistance=100k package=THT]
  R2 = Resistor [tolerance=±5% resistance=100k package=THT]
  R3 = Resistor [tolerance=±5% resistance=47k package=THT]
  R4 = Resistor [tolerance=±5% resistance=47k package=THT]
  Q1 = NPN-Transistor [part_number=2N3904 package="TO92 [THT]"]
  R5 = Resistor [tolerance=±5% resistance=4.7k package=THT]
  R6 = Resistor [tolerance=±5% resistance=10k package=THT]
  U3 = BNC [package=bnc]
  R7 = Trimmer Potentiometer [maximum_resistance=10kΩ package=THT]
  R8 = Resistor [tolerance=±5% resistance=150 package=THT]
  C1 = Ceramic Capacitor [capacitance=100nF package="100 mil [THT, multilayer]"]
  J2 = Power Jack [package=power_jack_pth]
  S1 = Pushbutton [package="[THT]"]
  S2 = Toggle Switch [package=THT]
  S3 = Pushbutton [package=THT]
  IC3 = IC, DIP package, 10 pins [chip_label=RCD]
  LED1 = LED - 3mm [color="Red (633nm)" package="3 mm [THT]"]
  R9 = Resistor [tolerance=±5% resistance=1k package=THT]
  R10 = Resistor [tolerance=±5% resistance=1k package=THT]
  LED2 = LED - 3mm [color="Yellow (592nm)" package="3 mm [THT]"]
  Q2 = PNP-Transistor [part_number=2N3906 package="TO92 [THT]"]

nets:
  N1: IC2.pin1, R8.Pin_1, C1.1
  N2: IC2.pin2, R7.wiper
  N3: IC2.pin3, IC3.pin1
  N4: IC2.pin5, U1.VOUT, R2.Pin_1
  GND: IC2.pin6, IC2.pin8, Part1.GND, J1.GND, U1.V-, U2.GND, R3.Pin_1, Q1.E, U3.GND, R7.leg1, C1.0, S1.Pin_2, S2.COM, IC3.pin4, LED1.cathode, LED2.cathode
  N5: IC2.pin9, Part1.D8
  N6: IC2.pin10, Part1.D7
  N7: IC2.pin12, IC2.pin15, Part1.D5
  N8: IC2.pin13, IC3.pin2, Q2.B
  N9: IC2.pin14, Q1.C, R5.Pin_1
  5V: IC2.pin16, Part1.5V, U1.V+, R4.Pin_0, R5.Pin_0, R7.leg2
  N10: Part1.D3, R8.Pin_0
  N11: Part1.D9, S2.L1
  N12: Part1.D10, S2.L2
  N13: Part1.D11/MOSI, S1.Pin_4
  12V: Part1.VIN, S3.leg0, IC3.pin5
  N14: J1.PWR, S3.leg1
  N15: U1.-IN, R1.Pin_1, R2.Pin_0
  N16: U1.+IN, R3.Pin_0, R4.Pin_1
  N17: U2.OUT, R1.Pin_0
  N18: Q1.B, R6.Pin_1
  N19: R6.Pin_0, U3.OUT
  N20: J2.GND, IC3.pin10
  N21: J2.PWR, IC3.pin6
  N22: IC3.pin3, R9.Pin_0, Q2.E
  N23: LED1.anode, R9.Pin_1
  N24: R10.Pin_0, Q2.C
  N25: R10.Pin_1, LED2.anode

notes:
  LED OUT
  Pwr. IN
  Mod. IN
  Trig. IN
  Inverter
  2 ch. multiplex
  Manual inputs
  19x31 holes
  Power IN
  On/Off
  ONOFF LED
  Emission LED

custom parts:
  MCP6241: low voltage audio power amplifier

// code stored in the sketch: ArdIllu.ino
/*
 Name:		ArdIllu.ino
 Created:	18/01/2020
 Author:	Francois Marelli, Idiap Research Institute <francois.marelli@idiap.ch>
*/

const unsigned short RESET_CODE = 0;
const unsigned short FIRMWARE_CODE = 1;
const unsigned short VERSION_CODE = 2;
const unsigned short TRIG_CODE = 3;
const unsigned short MOD_CODE = 4;
const unsigned short EXT_CODE = 5;

const unsigned char ACK = 0;
const unsigned char ERR = 1;
const unsigned char WARN = 2;

const unsigned long timeOut = 500;

const unsigned int version = 1;
const char firmware[] = "MM-ArdIllu";

const unsigned int switchPin = 9;
const unsigned int switchPinB = 10;
const unsigned int buttonPin = 11;


// Software control pins
const unsigned int trigPin = 5;
const unsigned int modPin = 3;

// Multiplexer control
const unsigned int multPinA = 7;
const unsigned int multPinB = 8;

bool manualMode = false;
bool isOn = false;
bool lastButtonState = true;

bool externalMode = false;

unsigned long lastDebounceTime = 0;
unsigned long debounceDelay = 50;

void setup() {
	pinMode(switchPin, INPUT_PULLUP);
	pinMode(switchPinB, INPUT_PULLUP);
	pinMode(buttonPin, INPUT_PULLUP);

	pinMode(trigPin, OUTPUT);
	pinMode(modPin, OUTPUT);
	
	pinMode(multPinA, OUTPUT);
	pinMode(multPinB, OUTPUT);

	reset();

	if (digitalRead(switchPin)){
		externalMode = true;
		digitalWrite(multPinA, HIGH);
		digitalWrite(multPinB, LOW);
	}
	else{
		externalMode = false;
		digitalWrite(multPinA, LOW);
		digitalWrite(multPinB, LOW);
  }

	Serial.begin(19200);
}

void loop() {
	bool switchReading = digitalRead(switchPin);

	if (switchReading && !externalMode){
		externalMode = true;
		digitalWrite(multPinA, HIGH);
		digitalWrite(multPinB, LOW);
	}

	else if (!switchReading && externalMode){
		externalMode = false;
		reset();
		digitalWrite(multPinA, LOW);
		digitalWrite(multPinB, LOW);
  }

	if (Serial.available() > 0) {
		int inByte = Serial.read();

		switch (inByte) {
				
		// Returns firmware name
		case FIRMWARE_CODE:
			Serial.println(firmware);
			break;

		// Returns version number
		case VERSION_CODE:
			Serial.println(version);
			break;

		// Returns 1 if external mode is on
		case EXT_CODE:
			Serial.println(externalMode);
		
		// Shut down the light
		case RESET_CODE:
			if (externalMode){
				Serial.write(WARN);
				break;
			}
			reset();
			break;

		// Set the trigger state
		case TRIG_CODE:
			if (externalMode){
				Serial.write(WARN);
				break;
			}
			if (waitForSerial(timeOut)) {
				if (manualMode){
					manualMode = false;
					digitalWrite(multPinA, LOW);
					digitalWrite(multPinB, LOW);
				}
				int value = Serial.read();
				digitalWrite(trigPin, value > 0);
				isOn = value > 0;
				Serial.write(ACK);
			}
			break;

		// Set the illumination power
		case MOD_CODE:
			if (externalMode){
				Serial.write(WARN);
				break;
			}
			if (waitForSerial(timeOut)) {
				if (manualMode){
					manualMode = false;
					digitalWrite(multPinA, LOW);
					digitalWrite(multPinB, LOW);
				}
				int value = Serial.read();
				analogWrite(modPin, 255 - value);
				Serial.write(ACK);
			}
			break;

    default:
        Serial.write(ERR);
		}
	}

	else if (!externalMode && !isOn){
		bool reading = digitalRead(buttonPin);
		if (reading != lastButtonState && (millis() - lastDebounceTime) > debounceDelay) {
			lastDebounceTime = millis();
			lastButtonState = reading;
			if (!reading) {
				manualMode = !manualMode;
				if (manualMode){					
					digitalWrite(multPinA, LOW);
					digitalWrite(multPinB, HIGH);
				}
				else {
					digitalWrite(multPinA, LOW);
					digitalWrite(multPinB, LOW);
				}
				digitalWrite(trigPin, manualMode);
			}
		}
	}
}

void reset() {
	digitalWrite(trigPin, LOW);
	analogWrite(modPin, 255);
	manualMode = false;
	isOn = false;
	if (!externalMode) {
		digitalWrite(multPinA, LOW);
		digitalWrite(multPinB, LOW);
	}
}

bool waitForSerial(unsigned long timeOut)
{
	unsigned long startTime = millis();
	while (Serial.available() == 0 && (millis() - startTime < timeOut)) {}
	if (Serial.available() > 0)
		return true;
	return false;
}

// code stored in the sketch: ArduinoIlluminatorFirmware.ino
/*
 Name:		ArdIllu.ino
 Created:	18/01/2020
 Author:	Francois Marelli, Idiap Research Institute <francois.marelli@idiap.ch>
*/

const unsigned short RESET_CODE = 0;
const unsigned short FIRMWARE_CODE = 1;
const unsigned short VERSION_CODE = 2;
const unsigned short SWITCH_CODE = 3;
const unsigned short INTENSITY_CODE = 4;
const unsigned short MODE_CODE = 5;

const unsigned char ACK = 0;
const unsigned char ERR = 1;

const unsigned long timeOut = 500;

const unsigned int version = 1;
const char firmware[] = "MM-ArdIllu";

const unsigned int switchPin = 9;
// const unsigned int switchPinB = 10;
const unsigned int buttonPin = 11;


// Software control pins
const unsigned int trigPin = 5;
const unsigned int modPin = 3;

// Multiplexer control
const unsigned int multPinA = 7;
const unsigned int multPinB = 8;

bool manualMode = false;
bool isOn = false;
bool lastButtonState = true;
bool buttonState = true;
bool externalMode;

unsigned long lastDebounceTime = 0;
unsigned long debounceDelay = 50;

void setup() {
	pinMode(switchPin, INPUT);
	pinMode(buttonPin, INPUT_PULLUP);

	pinMode(trigPin, OUTPUT);
	pinMode(modPin, OUTPUT);
	
	pinMode(multPinA, OUTPUT);
	pinMode(multPinB, OUTPUT);

	reset();

	if (digitalRead(switchPin)){
		externalMode = true;
		digitalWrite(multPinA, HIGH);
		digitalWrite(multPinB, LOW);
	}
	else{
		externalMode = false;
		digitalWrite(multPinA, LOW);
		digitalWrite(multPinB, LOW);
  }

	Serial.begin(19200);
}

void loop() {
	if (Serial.available() > 0) {
		int inByte = Serial.read();

		switch (inByte) {
		
		// Shut down the light
		case RESET_CODE:
			reset();
			break;
		
		// Returns firmware name
		case FIRMWARE_CODE:
			Serial.println(firmware);
			break;

		// Returns version number
		case VERSION_CODE:
			Serial.println(version);
			break;

		// Set the switch state
		case SWITCH_CODE:
			if (waitForSerial(timeOut)) {
				manualMode = false;
				int value = Serial.read();
				digitalWrite(switchPin, value > 0);
				isOn = value > 0;
				Serial.write(ACK);
			}
			break;

		// Set the illumination power
		case INTENSITY_CODE:
			if (waitForSerial(timeOut)) {
				manualMode = false;
				int value = Serial.read();
				analogWrite(intensityPin, 255 - value);
				Serial.write(ACK);
			}
			break;

    default:
        Serial.write(ERR);						
		}
	}

	else if (!externalMode && !isOn){
		bool reading = digitalRead(buttonPin);

		if (reading != lastButtonState && (millis() - lastDebounceTime) > debounceDelay) {
			lastDebounceTime = millis();
			lastButtonState = reading;

			if (!reading) {
				manualMode = !manualMode;
				if (manualMode){
					
				}
				digitalWrite(trigPin, manualMode);
				
			}
		}

		if (manualMode){
			int value = analogRead(controlPin);
			analogWrite(intensityPin, value/4);
		}
	}
}

void reset() {
	digitalWrite(switchPin, LOW);
	analogWrite(intensityPin, 255);
	manualMode = false;
	isOn = false;
}

bool waitForSerial(unsigned long timeOut)
{
	unsigned long startTime = millis();
	while (Serial.available() == 0 && (millis() - startTime < timeOut)) {}
	if (Serial.available() > 0)
		return true;
	return false;
}
